// Logisim project Milestone2.circ as structural Verilog: 12 circuits, main circuit main
module main (
);

  wire alu_ctrl_1_alu_src, and_1_out, Clock, comparator_1_eq, control_1_branch, control_1_mem_read,
       control_1_mem_to_reg, control_1_mem_write, control_1_reg_write;
  wire [3:0] alu_ctrl_1_alu_ctrl;
  wire [31:0] adder_1_out, adder_2_out, alu32_1_r, datamemory_1_readdata, IMM32,
       instructionmemory_1_instruction, multiplexer_1_out, multiplexer_2_out, multiplexer_3_out,
       register_1_q, register_file_1_r_data1, register_file_1_r_data2;

  Clock clock_1 (.out(Clock));
  Register #(.width(32)) register_1 (.D(multiplexer_1_out), .en(1'b1), .clk(Clock), .Q(register_1_q));  // open: clr
  Adder #(.width(32)) adder_1 (.a(register_1_q), .b(32'h4), .out(adder_1_out));  // open: cin, cout
  Adder #(.width(32)) adder_2 (.a(register_1_q), .b(IMM32), .out(adder_2_out));  // open: cin, cout
  Multiplexer #(.enable("false"), .width(32)) multiplexer_1 (
    .in0(adder_1_out), .in1(adder_2_out), .out(multiplexer_1_out), .sel(and_1_out));
  InstructionMemory instructionmemory_1 (
    .Address(register_1_q[23:0]), .ClockIn(Clock), .Instruction(instructionmemory_1_instruction));
  Control control_1 (
    .l0(instructionmemory_1_instruction[0]), .l1(instructionmemory_1_instruction[1]),
    .l2(instructionmemory_1_instruction[2]), .l3(instructionmemory_1_instruction[3]),
    .l4(instructionmemory_1_instruction[4]), .l5(instructionmemory_1_instruction[5]),
    .l6(instructionmemory_1_instruction[6]), .mem_to_reg(control_1_mem_to_reg),
    .reg_write(control_1_reg_write), .mem_read(control_1_mem_read), .mem_write(control_1_mem_write),
    .branch(control_1_branch));
  register_file register_file_1 (
    .W_Data(multiplexer_3_out), .Clock_In(Clock), .R_Reg1(instructionmemory_1_instruction[19:15]),
    .R_Reg2(instructionmemory_1_instruction[24:20]), .Write(control_1_reg_write),
    .W_Reg(instructionmemory_1_instruction[11:7]), .R_Data1(register_file_1_r_data1),
    .R_Data2(register_file_1_r_data2));
  ImmGen immgen_1 (.Instruction(instructionmemory_1_instruction), .IMM32(IMM32));
  ALU_Ctrl alu_ctrl_1 (
    .l30(instructionmemory_1_instruction[30]), .l14(instructionmemory_1_instruction[14]),
    .l13(instructionmemory_1_instruction[13]), .l12(instructionmemory_1_instruction[12]),
    .l6(instructionmemory_1_instruction[6]), .l5(instructionmemory_1_instruction[5]),
    .l4(instructionmemory_1_instruction[4]), .ALU_Ctrl(alu_ctrl_1_alu_ctrl), .ALU_Src(alu_ctrl_1_alu_src));
  Comparator #(.width(32)) comparator_1 (
    .a(register_file_1_r_data1), .b(register_file_1_r_data2), .eq(comparator_1_eq));  // open: gt, lt
  and and_1 (and_1_out, control_1_branch, comparator_1_eq);
  Multiplexer #(.enable("false"), .width(32)) multiplexer_2 (
    .in0(register_file_1_r_data2), .in1(IMM32), .out(multiplexer_2_out), .sel(alu_ctrl_1_alu_src));
  ALU32 alu32_1 (
    .ALU_Ctrl(alu_ctrl_1_alu_ctrl), .A(register_file_1_r_data1), .B(multiplexer_2_out), .R(alu32_1_r));  // open: C_Out
  Multiplexer #(.enable("false"), .width(32)) multiplexer_3 (
    .in0(alu32_1_r), .in1(datamemory_1_readdata), .out(multiplexer_3_out), .sel(control_1_mem_to_reg));
  DataMemory datamemory_1 (
    .Address(alu32_1_r[25:0]), .MemWrite(control_1_mem_write), .MemRead(control_1_mem_read), .ClockIn(Clock),
    .WriteData(register_file_1_r_data2), .ReadData(datamemory_1_readdata));
endmodule

module ImmGen (
  input  [31:0] Instruction,
  output [31:0] IMM32
);

  Multiplexer #(.enable("false"), .select(2)) multiplexer_1 (
    .in0(Instruction[20]), .in1(Instruction[7]), .in3(1'b0), .out(IMM32[0]), .sel(Instruction[6:5]));  // open: in2
  Multiplexer #(.enable("false"), .width(4)) multiplexer_2 (
    .in0(Instruction[24:21]), .in1(Instruction[11:8]), .out(IMM32[4:1]), .sel(Instruction[5]));
  Multiplexer #(.enable("false")) multiplexer_3 (
    .in0(Instruction[31]), .in1(Instruction[7]), .out(IMM32[11]), .sel(Instruction[6]));
  assign IMM32[31:12] = {{19{Instruction[31]}}, Instruction[31]};  // Bit_Extender bit_extender_1

  assign IMM32[10:5] = Instruction[30:25];

  // Other names for the same wires on the sheet: l25_30[5:0] = Instruction[30:25]; l5 = Instruction[5];
  //   l6_5[1:0] = Instruction[6:5]; l6 = Instruction[6]; l7 = Instruction[7]; l8_11[3:0] = Instruction[11:8];
  //   l20 = Instruction[20]; l21_24[3:0] = Instruction[24:21]; l31 = Instruction[31]
endmodule

module Control (
  input  l0,
  input  l1,
  input  l2,
  input  l3,
  input  l4,
  input  l5,
  input  l6,
  output mem_to_reg,
  output reg_write,
  output mem_read,
  output mem_write,
  output branch
);

  wire not_2_out, not_3_out;

  not not_1 (mem_to_reg, l4);
  not not_2 (not_2_out, l5);
  not not_3 (not_3_out, l6);
  or or_1 (reg_write, not_2_out, l4);
  and and_1 (mem_read, mem_to_reg, not_2_out);
  and and_2 (mem_write, mem_to_reg, l5, not_3_out);

  assign branch = l6;
endmodule

module InstructionMemory (
  input  [23:0] Address,
  input  ClockIn,
  output [31:0] Instruction
);

  wire not_1_out;

  RAM #(.addrWidth(22), .asyncread("true"), .dataWidth(32)) ram_1 (
    .addr(Address[23:2]), .we(1'b0), .oe(not_1_out), .dout(Instruction));  // open: clk, din
  not not_1 (not_1_out, ClockIn);
endmodule

module DataMemory (
  input  [25:0] Address,
  input  MemWrite,
  input  MemRead,
  input  ClockIn,
  input  [31:0] WriteData,
  output [31:0] ReadData
);

  RAM #(.addrWidth(24), .asyncread("true"), .dataWidth(32)) ram_1 (
    .addr(Address[25:2]), .we(MemWrite), .oe(MemRead), .clk(ClockIn), .din(WriteData), .dout(ReadData));
endmodule

module register_file (
  input  [31:0] W_Data,
  input  Clock_In,
  input  [4:0] R_Reg1,
  input  [4:0] R_Reg2,
  input  Write,
  input  [4:0] W_Reg,
  output [31:0] R_Data1,
  output [31:0] R_Data2
);

  wire R0, R1, R2, R3, R4, R5, R6, R7, R8, R9, R10, R11, R12, R13, R14, R15, R16, R17, R18, R19, R20, R21,
       R22, R23, R24, R25, R26, R27, R28, R29, R30, R31;
  wire [31:0] Q0, Q1, Q2, Q3, Q4, Q5, Q6, Q7, Q8, Q9, Q10, Q11, Q12, Q13, Q14, Q15, Q16, Q17, Q18, Q19, Q20,
       Q21, Q22, Q23, Q24, Q25, Q26, Q27, Q28, Q29, Q30, Q31;

  Demultiplexer #(.enable("false"), .select(5)) demultiplexer_1 (
    .out0(R0), .out1(R1), .out2(R2), .out3(R3), .out4(R4), .out5(R5), .out6(R6), .out7(R7), .out8(R8),
    .out9(R9), .out10(R10), .out11(R11), .out12(R12), .out13(R13), .out14(R14), .out15(R15), .out16(R16),
    .out17(R17), .out18(R18), .out19(R19), .out20(R20), .out21(R21), .out22(R22), .out23(R23), .out24(R24),
    .out25(R25), .out26(R26), .out27(R27), .out28(R28), .out29(R29), .out30(R30), .out31(R31), .in(Write),
    .sel(W_Reg));
  Register #(.width(32)) register_1 (.D(W_Data), .en(R0), .clk(Clock_In), .Q(Q0), .clr(Write));
  Register #(.width(32)) register_2 (.D(W_Data), .en(R1), .clk(Clock_In), .Q(Q1));  // open: clr
  Register #(.width(32)) register_3 (.D(W_Data), .en(R2), .clk(Clock_In), .Q(Q2));  // open: clr
  Register #(.width(32)) register_4 (.D(W_Data), .en(R3), .clk(Clock_In), .Q(Q3));  // open: clr
  Register #(.width(32)) register_5 (.D(W_Data), .en(R4), .clk(Clock_In), .Q(Q4));  // open: clr
  Register #(.width(32)) register_6 (.D(W_Data), .en(R5), .clk(Clock_In), .Q(Q5));  // open: clr
  Register #(.width(32)) register_7 (.D(W_Data), .en(R6), .clk(Clock_In), .Q(Q6));  // open: clr
  Register #(.width(32)) register_8 (.D(W_Data), .en(R7), .clk(Clock_In), .Q(Q7));  // open: clr
  Register #(.width(32)) register_9 (.D(W_Data), .en(R8), .clk(Clock_In), .Q(Q8));  // open: clr
  Register #(.width(32)) register_10 (.D(W_Data), .en(R9), .clk(Clock_In), .Q(Q9));  // open: clr
  Register #(.width(32)) register_11 (.D(W_Data), .en(R10), .clk(Clock_In), .Q(Q10));  // open: clr
  Register #(.width(32)) register_12 (.D(W_Data), .en(R11), .clk(Clock_In), .Q(Q11));  // open: clr
  Register #(.width(32)) register_13 (.D(W_Data), .en(R12), .clk(Clock_In), .Q(Q12));  // open: clr
  Register #(.width(32)) register_14 (.D(W_Data), .en(R13), .clk(Clock_In), .Q(Q13));  // open: clr
  Register #(.width(32)) register_15 (.D(W_Data), .en(R14), .clk(Clock_In), .Q(Q14));  // open: clr
  Register #(.width(32)) register_16 (.D(W_Data), .en(R15), .clk(Clock_In), .Q(Q15));  // open: clr
  Register #(.width(32)) register_17 (.D(W_Data), .en(R16), .clk(Clock_In), .Q(Q16));  // open: clr
  Register #(.width(32)) register_18 (.D(W_Data), .en(R17), .clk(Clock_In), .Q(Q17));  // open: clr
  Register #(.width(32)) register_19 (.D(W_Data), .en(R18), .clk(Clock_In), .Q(Q18));  // open: clr
  Register #(.width(32)) register_20 (.D(W_Data), .en(R19), .clk(Clock_In), .Q(Q19));  // open: clr
  Register #(.width(32)) register_21 (.D(W_Data), .en(R20), .clk(Clock_In), .Q(Q20));  // open: clr
  Register #(.width(32)) register_22 (.D(W_Data), .en(R21), .clk(Clock_In), .Q(Q21));  // open: clr
  Register #(.width(32)) register_23 (.D(W_Data), .en(R22), .clk(Clock_In), .Q(Q22));  // open: clr
  Register #(.width(32)) register_24 (.D(W_Data), .en(R23), .clk(Clock_In), .Q(Q23));  // open: clr
  Register #(.width(32)) register_25 (.D(W_Data), .en(R24), .clk(Clock_In), .Q(Q24));  // open: clr
  Register #(.width(32)) register_26 (.D(W_Data), .en(R25), .clk(Clock_In), .Q(Q25));  // open: clr
  Register #(.width(32)) register_27 (.D(W_Data), .en(R26), .clk(Clock_In), .Q(Q26));  // open: clr
  Register #(.width(32)) register_28 (.D(W_Data), .en(R27), .clk(Clock_In), .Q(Q27));  // open: clr
  Register #(.width(32)) register_29 (.D(W_Data), .en(R28), .clk(Clock_In), .Q(Q28));  // open: clr
  Register #(.width(32)) register_30 (.D(W_Data), .en(R29), .clk(Clock_In), .Q(Q29));  // open: clr
  Register #(.width(32)) register_31 (.D(W_Data), .en(R30), .clk(Clock_In), .Q(Q30));  // open: clr
  Register #(.width(32)) register_32 (.D(W_Data), .en(R31), .clk(Clock_In), .Q(Q31));  // open: clr
  Multiplexer #(.enable("false"), .select(5), .width(32)) multiplexer_1 (
    .in0(Q0), .in1(Q1), .in2(Q2), .in3(Q3), .in4(Q4), .in5(Q5), .in6(Q6), .in7(Q7), .in8(Q8), .in9(Q9),
    .in10(Q10), .in11(Q11), .in12(Q12), .in13(Q13), .in14(Q14), .in15(Q15), .in16(Q16), .in17(Q17),
    .in18(Q18), .in19(Q19), .in20(Q20), .in21(Q21), .in22(Q22), .in23(Q23), .in24(Q24), .in25(Q25),
    .in26(Q26), .in27(Q27), .in28(Q28), .in29(Q29), .in30(Q30), .in31(Q31), .out(R_Data1), .sel(R_Reg1));
  Multiplexer #(.enable("false"), .select(5), .width(32)) multiplexer_2 (
    .in0(Q0), .in1(Q1), .in2(Q2), .in3(Q3), .in4(Q4), .in5(Q5), .in6(Q6), .in7(Q7), .in8(Q8), .in9(Q9),
    .in10(Q10), .in11(Q11), .in12(Q12), .in13(Q13), .in14(Q14), .in15(Q15), .in16(Q16), .in17(Q17),
    .in18(Q18), .in19(Q19), .in20(Q20), .in21(Q21), .in22(Q22), .in23(Q23), .in24(Q24), .in25(Q25),
    .in26(Q26), .in27(Q27), .in28(Q28), .in29(Q29), .in30(Q30), .in31(Q31), .out(R_Data2), .sel(R_Reg2));
endmodule

module ALU_Ctrl (
  input  l30,
  input  l14,
  input  l13,
  input  l12,
  input  l6,
  input  l5,
  input  l4,
  output [3:0] ALU_Ctrl,
  output ALU_Src
);

  wire and_2_out, not_1_out, not_2_out, not_3_out, not_4_out, not_5_out;

  not not_1 (not_1_out, l14);
  not not_2 (not_2_out, l13);
  not not_3 (not_3_out, l12);
  not not_4 (not_4_out, l5);
  not not_5 (not_5_out, l4);
  and and_1 (ALU_Ctrl[2], l30, not_2_out, l5);
  or or_1 (ALU_Ctrl[1], not_2_out, not_5_out);
  and and_2 (and_2_out, l13, not_3_out);
  or or_2 (ALU_Src, not_4_out, not_5_out);
  or or_3 (ALU_Ctrl[0], not_1_out, and_2_out);

  assign ALU_Ctrl[3] = 1'b0;
endmodule

module one_bit_adder (
  input  A,
  input  B,
  input  C_In,
  output S,
  output C_Out
);

  wire and_1_out, and_2_out, and_3_out, and_4_out, and_5_out, and_6_out, and_7_out, not_1_out, not_2_out,
       not_3_out;

  not not_1 (not_1_out, A);
  not not_2 (not_2_out, B);
  not not_3 (not_3_out, C_In);
  and and_1 (and_1_out, not_1_out, not_2_out, C_In);
  and and_2 (and_2_out, not_1_out, B, not_3_out);
  and and_3 (and_3_out, A, not_2_out, not_3_out);
  and and_4 (and_4_out, A, B, C_In);
  and and_5 (and_5_out, B, C_In);
  and and_6 (and_6_out, A, C_In);
  and and_7 (and_7_out, A, B);
  or or_1 (S, and_1_out, and_2_out, and_3_out, and_4_out);
  or or_2 (C_Out, and_5_out, and_6_out, and_7_out);
endmodule

module one_bit_ALU (
  input  [3:0] ALU_Ctrl,
  input  A,
  input  B,
  input  C_In,
  output R,
  output C_Out
);

  wire and_1_out, multiplexer_1_out, not_1_out, one_bit_adder_1_s, or_1_out, xor_1_out;

  not not_1 (not_1_out, B);
  Multiplexer #(.enable("false")) multiplexer_1 (.in0(B), .in1(not_1_out), .out(multiplexer_1_out), .sel(ALU_Ctrl[2]));
  and and_1 (and_1_out, A, multiplexer_1_out);
  or or_1 (or_1_out, A, multiplexer_1_out);
  xor xor_1 (xor_1_out, A, multiplexer_1_out);
  one_bit_adder one_bit_adder_1 (.A(A), .B(multiplexer_1_out), .C_In(C_In), .S(one_bit_adder_1_s), .C_Out(C_Out));
  Multiplexer #(.enable("false"), .select(2)) multiplexer_2 (
    .in0(and_1_out), .in1(or_1_out), .in2(xor_1_out), .in3(one_bit_adder_1_s), .out(R), .sel(ALU_Ctrl[1:0]));
endmodule

module four_bit_ALU (
  input  [3:0] ALU_Ctrl,
  input  [3:0] A,
  input  [3:0] B,
  input  C_In,
  output [3:0] R,
  output C_Out
);

  wire one_bit_alu_1_c_out, one_bit_alu_2_c_out, one_bit_alu_3_c_out;

  one_bit_ALU one_bit_alu_1 (
    .ALU_Ctrl(ALU_Ctrl), .A(A[0]), .B(B[0]), .C_In(C_In), .R(R[0]), .C_Out(one_bit_alu_1_c_out));
  one_bit_ALU one_bit_alu_2 (
    .ALU_Ctrl(ALU_Ctrl), .A(A[1]), .B(B[1]), .C_In(one_bit_alu_1_c_out), .R(R[1]), .C_Out(one_bit_alu_2_c_out));
  one_bit_ALU one_bit_alu_3 (
    .ALU_Ctrl(ALU_Ctrl), .A(A[2]), .B(B[2]), .C_In(one_bit_alu_2_c_out), .R(R[2]), .C_Out(one_bit_alu_3_c_out));
  one_bit_ALU one_bit_alu_4 (
    .ALU_Ctrl(ALU_Ctrl), .A(A[3]), .B(B[3]), .C_In(one_bit_alu_3_c_out), .R(R[3]), .C_Out(C_Out));
endmodule

module ALU32 (
  input  [3:0] ALU_Ctrl,
  input  [31:0] A,
  input  [31:0] B,
  output [31:0] R,
  output C_Out
);

  wire sixteen_bit_alu_1_c_out;

  sixteen_bit_ALU sixteen_bit_alu_1 (
    .ALU_Ctrl(ALU_Ctrl), .A(A[15:0]), .B(B[15:0]), .R(R[15:0]), .C_Out(sixteen_bit_alu_1_c_out));  // open: C_In
  sixteen_bit_ALU sixteen_bit_alu_2 (
    .ALU_Ctrl(ALU_Ctrl), .A(A[31:16]), .B(B[31:16]), .C_In(sixteen_bit_alu_1_c_out), .R(R[31:16]),
    .C_Out(C_Out));
endmodule

module sixteen_bit_ALU (
  input  [3:0] ALU_Ctrl,
  input  [15:0] A,
  input  [15:0] B,
  input  C_In,
  output [15:0] R,
  output C_Out
);

  wire four_bit_alu_1_c_out, four_bit_alu_2_c_out, four_bit_alu_3_c_out;

  four_bit_ALU four_bit_alu_1 (
    .ALU_Ctrl(ALU_Ctrl), .A(A[3:0]), .B(B[3:0]), .C_In(C_In), .R(R[3:0]), .C_Out(four_bit_alu_1_c_out));
  four_bit_ALU four_bit_alu_2 (
    .ALU_Ctrl(ALU_Ctrl), .A(A[7:4]), .B(B[7:4]), .C_In(four_bit_alu_1_c_out), .R(R[7:4]),
    .C_Out(four_bit_alu_2_c_out));
  four_bit_ALU four_bit_alu_3 (
    .ALU_Ctrl(ALU_Ctrl), .A(A[11:8]), .B(B[11:8]), .C_In(four_bit_alu_2_c_out), .R(R[11:8]),
    .C_Out(four_bit_alu_3_c_out));
  four_bit_ALU four_bit_alu_4 (
    .ALU_Ctrl(ALU_Ctrl), .A(A[15:12]), .B(B[15:12]), .C_In(four_bit_alu_3_c_out), .R(R[15:12]), .C_Out(C_Out));
endmodule
